// Digital circuit  instruction-memory.dig as structural Verilog
module instruction_memory (
  input  [7:0] A,
  input  [1:0] PROG,
  output [31:0] D
);

  wire [31:0] fib_rec_d, get_bitseq_d, is_palrec_d, quadratic_d;

  ROM #(.AddrBits(8), .Bits(32)) fib_rec (.A(A), .sel(1'b1), .D(fib_rec_d));
  ROM #(.AddrBits(8), .Bits(32)) is_palrec (.A(A), .sel(1'b1), .D(is_palrec_d));
  ROM #(.AddrBits(8), .Bits(32)) get_bitseq (.A(A), .sel(1'b1), .D(get_bitseq_d));
  ROM #(.AddrBits(8), .Bits(32)) quadratic (.A(A), .sel(1'b1), .D(quadratic_d));
  Multiplexer #(.Selector_Bits(2), .Bits(32)) multiplexer_1 (
    .sel(PROG), .in_0(fib_rec_d), .in_1(is_palrec_d), .in_2(get_bitseq_d), .in_3(quadratic_d), .out(D));

  // Notes on the sheet:
  //   contents of fib_rec (hex, n*v repeats v):
  //   100293,a2c463,8067,fe810113,113023,a13423,fff50513,fe5ff0ef,a13823
  //   ,813503,ffe50513,fd5ff0ef,1013303,650533,13083,1810113,8067,c0001073
  //   contents of is_palrec (hex, n*v repeats v):
  //   c5c663,100513,3c0006f,b502b3,28283,c50333,30303,628663,513,200006f
  //   ,ff810113,113023,158593,fff60613,fc9ff0ef,13083,810113,8067,c0001073
  //   contents of get_bitseq (hex, n*v repeats v):
  //   40b602b3,128293,4000393,729863,50313,fff00393,140006f,b55333,100393
  //   ,5393b3,fff38393,737533,8067,c0001073
  //   contents of quadratic (hex, n*v repeats v):
  //   2a502b3,2b282b3,2c50333,628533,d50533,8067,c0001073
endmodule
