// Digital circuit 1-bit-register.dig as structural Verilog
module _1_bit_register (
  input  D,
  input  CLK,
  input  EN,
  input  CLR,
  output Q,
  output nQ
);

  wire d_latch_clr_1_q, multiplexer_1_out, not_1_out;

  Multiplexer multiplexer_1 (.sel(EN), .in_0(Q), .in_1(D), .out(multiplexer_1_out));
  not not_1 (not_1_out, CLK);
  d_latch_clr d_latch_clr_1 (.Q(d_latch_clr_1_q), .D(multiplexer_1_out), .CLK(not_1_out), .CLR(CLR));  // open: nQ
  d_latch_clr d_latch_clr_2 (.Q(Q), .nQ(nQ), .D(d_latch_clr_1_q), .CLK(CLK), .CLR(CLR));
endmodule
