// Digital circuit 4bit-register-clr-en.dig as structural Verilog
module _4bit_register_clr_en (
  input  [3:0] D,
  input  CLK,
  input  EN,
  input  CLR,
  output [3:0] Q
);

  _2_bit_register_clr_en _2_bit_register_clr_en_1 (.D(D[1:0]), .CLK(CLK), .EN(EN), .CLR(CLR), .Q(Q[1:0]));
  _2_bit_register_clr_en _2_bit_register_clr_en_2 (.D(D[3:2]), .CLK(CLK), .EN(EN), .CLR(CLR), .Q(Q[3:2]));
endmodule
