// Digital circuit ADDR.dig as structural Verilog
module ADDR (
  input  [6:0] iw_opcode,
  input  [2:0] iw_funct3,
  input  [6:0] iw_funct7,
  input  [6:0] opcode,
  input  [2:0] funct3,
  input  [6:0] funct7,
  output eq
);

  wire add_2_eq, add_eq, r_type_eq;

  Comparator #(.Bits(7)) r_type (.a(iw_opcode), .b(opcode), .eq(r_type_eq));  // open: gt, lt
  Comparator #(.Bits(3)) add (.a(iw_funct3), .b(funct3), .eq(add_eq));  // open: gt, lt
  Comparator #(.Bits(7)) add_2 (.a(iw_funct7), .b(funct7), .eq(add_2_eq));  // open: gt, lt
  and and_1 (eq, r_type_eq, add_eq, add_2_eq);
endmodule
