// Digital circuit AND.dig as structural Verilog
module AND (
  input  [6:0] OPC,
  input  [2:0] funct3,
  input  [6:0] funct7,
  output eq
);

  wire AND_eq, comparator_1_eq, comparator_2_eq;

  Comparator #(.Bits(7)) AND (.a(OPC), .b(7'b0110011), .eq(AND_eq));  // open: gt, lt
  Comparator #(.Bits(3)) comparator_1 (.a(funct3), .b(3'b111), .eq(comparator_1_eq));  // open: gt, lt
  Comparator #(.Bits(7)) comparator_2 (.a(funct7), .b({7{1'b0}}), .eq(comparator_2_eq));  // open: gt, lt
  and and_2 (eq, AND_eq, comparator_1_eq, comparator_2_eq);
endmodule
