// Digital circuit BGE.dig as structural Verilog
module BGE (
  input  [6:0] OPC,
  input  [2:0] funct3,
  output eq
);

  wire BEQ_eq, comparator_1_eq;

  Comparator #(.Bits(7)) BEQ (.a(OPC), .b(7'b1100011), .eq(BEQ_eq));  // open: gt, lt
  Comparator #(.Bits(3)) comparator_1 (.a(funct3), .b(3'b101), .eq(comparator_1_eq));  // open: gt, lt
  and and_1 (eq, BEQ_eq, comparator_1_eq);
endmodule
