// Digital circuit BLT.dig as structural Verilog
module BLT (
  input  [6:0] OPC,
  input  [2:0] funct3,
  output eq
);

  wire BLT_eq, comparator_1_eq;

  Comparator #(.Bits(7)) BLT (.a(OPC), .b(7'b1100011), .eq(BLT_eq));  // open: gt, lt
  Comparator #(.Bits(3)) comparator_1 (.a(funct3), .b(3'b100), .eq(comparator_1_eq));  // open: gt, lt
  and and_1 (eq, BLT_eq, comparator_1_eq);
endmodule
