// Digital circuit BU.dig as structural Verilog
module BU (
  input  [63:0] RD0,
  input  [1:0] BRop,
  input  [63:0] RD1,
  output PCbr
);

  wire and_1_out, beq_eq, bge_eq, bge_gt, blt_lt, bne_eq, not_1_out;

  Comparator #(.Bits(64)) beq (.a(RD0), .b(RD1), .eq(beq_eq));  // open: gt, lt
  Comparator #(.Bits(64)) bne (.a(RD0), .b(RD1), .eq(bne_eq));  // open: gt, lt
  Comparator #(.Bits(64)) blt (.a(RD0), .b(RD1), .lt(blt_lt));  // open: gt, eq
  Comparator #(.Bits(64)) bge (.a(RD0), .b(RD1), .gt(bge_gt), .eq(bge_eq));  // open: lt
  not not_1 (not_1_out, bne_eq);
  and and_1 (and_1_out, bge_gt, bge_eq);
  Multiplexer #(.Selector_Bits(2)) multiplexer_1 (
    .sel(BRop), .in_0(beq_eq), .in_1(not_1_out), .in_2(blt_lt), .in_3(and_1_out), .out(PCbr));
endmodule
