// Digital circuit ImmDecoder.dig as structural Verilog
module ImmDecoder (
  input  [31:0] IW,
  output [63:0] imm_S,
  output [63:0] imm_I,
  output [63:0] imm_B,
  output [63:0] imm_U,
  output [63:0] imm_J
);

  BitExtender #(.inputBits(12), .outputBits(64)) _12_bits (.in(IW[31:20]), .out(imm_I));
  BitExtender #(.inputBits(12), .outputBits(64)) _12_bits_2 (.in({IW[31:25], IW[11:7]}), .out(imm_S));
  BitExtender #(.inputBits(32), .outputBits(64)) bitextender_1 (.in(IW), .out(imm_B));
  BitExtender #(.inputBits(32), .outputBits(64)) bitextender_2 (.in(IW), .out(imm_U));
  BitExtender #(.inputBits(21), .outputBits(64)) _21_bits (
    .in({1'b0, IW[19:12], IW[20], IW[30:21], IW[31]}), .out(imm_J));
endmodule
