// Digital circuit InstDecoder.dig as structural Verilog
module InstDecoder (
  input  [31:0] IW,
  output [2:0] ALUSrcB,
  output [3:0] ALUOp,
  output RFW,
  output [1:0] WDsel,
  output [1:0] PCsel,
  output ALUSrcA,
  output [1:0] BROp,
  output MST,
  output MLD,
  output [1:0] MSZ
);

  wire addi_1_eq, addr_1_eq, and_1_eq, beq_1_eq, bge_1_eq, blt_1_eq, bne_1_eq, j_type_eq, jalr_1_eq, lb_1_eq,
       ld_1_eq, lw_1_eq, mul_1_eq, or_1_eq, sb_1_eq, sd_1_eq, sll_1_r, slli_1_r, srai_1_eq, srl_1_eq,
       srli_1_r, sub_1_r, sw_1_eq;
  wire [4:0] INUM_num;

  ADDI addi_1 (.iw_opcode(IW[6:0]), .iw_funct3(IW[14:12]), .eq(addi_1_eq));
  ADDR addr_1 (.iw_opcode(IW[6:0]), .iw_funct3(IW[14:12]), .iw_funct7(IW[31:25]), .eq(addr_1_eq));
  Comparator #(.Bits(7)) j_type (.a(IW[6:0]), .b(7'b1101111), .eq(j_type_eq));  // open: gt, lt
  JALR jalr_1 (.iw_opcode(IW[6:0]), .iw_funct3(IW[14:12]), .eq(jalr_1_eq));
  MUL mul_1 (.OPC(IW[6:0]), .funct3(IW[14:12]), .funct7(IW[31:25]), .eq(mul_1_eq));
  SUB sub_1 (.OPC(IW[6:0]), .funct3(IW[14:12]), .funct7(IW[31:25]), .R(sub_1_r));
  SLL sll_1 (.OPC(IW[6:0]), .funct3(IW[14:12]), .funct7(IW[31:25]), .R(sll_1_r));
  SRL srl_1 (.OPC(IW[6:0]), .funct3(IW[14:12]), .funct7(IW[31:25]), .eq(srl_1_eq));
  SLLI slli_1 (.OPC(IW[6:0]), .funct3(IW[14:12]), .funct7(IW[31:25]), .R(slli_1_r));
  SRLI srli_1 (.OPC(IW[6:0]), .funct3(IW[14:12]), .funct7(IW[31:25]), .R(srli_1_r));
  SRAI srai_1 (.OPC(IW[6:0]), .funct3(IW[14:12]), .funct7(IW[31:25]), .eq(srai_1_eq));
  BEQ beq_1 (.OPC(IW[6:0]), .funct3(IW[14:12]), .eq(beq_1_eq));
  BNE bne_1 (.OPC(IW[6:0]), .funct3(IW[14:12]), .eq(bne_1_eq));
  BLT blt_1 (.OPC(IW[6:0]), .funct3(IW[14:12]), .eq(blt_1_eq));
  BGE bge_1 (.OPC(IW[6:0]), .funct3(IW[14:12]), .eq(bge_1_eq));
  LD ld_1 (.OPC(IW[6:0]), .funct3(IW[14:12]), .eq(ld_1_eq));
  LW lw_1 (.OPC(IW[6:0]), .funct3(IW[14:12]), .eq(lw_1_eq));
  LB lb_1 (.OPC(IW[6:0]), .funct3(IW[14:12]), .eq(lb_1_eq));
  SD sd_1 (.OPC(IW[6:0]), .funct3(IW[14:12]), .eq(sd_1_eq));
  SW sw_1 (.OPC(IW[6:0]), .funct3(IW[14:12]), .eq(sw_1_eq));
  SB sb_1 (.OPC(IW[6:0]), .funct3(IW[14:12]), .eq(sb_1_eq));
  AND and_1 (.OPC(IW[6:0]), .funct3(IW[14:12]), .funct7(IW[31:25]), .eq(and_1_eq));
  OR or_1 (.OPC(IW[6:0]), .funct3(IW[14:12]), .funct7(IW[31:25]), .eq(or_1_eq));
  PriorityEncoder #(.Selector_Bits(5)) INUM (
    .in0(addi_1_eq), .in1(addr_1_eq), .in2(j_type_eq), .in3(jalr_1_eq), .in4(mul_1_eq), .in5(sub_1_r),
    .in6(sll_1_r), .in7(srl_1_eq), .in8(slli_1_r), .in9(srli_1_r), .in10(srai_1_eq), .in11(beq_1_eq),
    .in12(bne_1_eq), .in13(blt_1_eq), .in14(bge_1_eq), .in15(ld_1_eq), .in16(lw_1_eq), .in17(lb_1_eq),
    .in18(sd_1_eq), .in19(sw_1_eq), .in20(sb_1_eq), .in21(and_1_eq), .in22(or_1_eq), .in23(1'b0),
    .in24(1'b0), .in25(1'b0), .in26(1'b0), .in27(1'b0), .in28(1'b0), .in29(1'b0), .in30(1'b0), .in31(1'b0),
    .num(INUM_num));  // open: any
  ROM #(.AddrBits(5), .Bits(19)) rom_1 (
    .A(INUM_num), .sel(1'b1), .D({RFW, ALUOp, ALUSrcA, ALUSrcB, PCsel, WDsel, BROp, MST, MLD, MSZ}));

  // Other names for the same wires on the sheet: iw_opcode[6:0] = IW[6:0]; iw_f3[2:0] = IW[14:12];
  //   iw_f7[6:0] = IW[31:25]

  // Notes on the sheet:
  //   contents of rom_1 (hex, n*v repeats v):
  //   40400,40000,42d40,40540,44000,48000,4c000,50000,54400,58400,5c400
  //   ,2a00,2a10,2a20,2a30,40484,40485,40486,100c,100d,100e,60000,64000
endmodule
