// Digital circuit JALR.dig as structural Verilog
module JALR (
  input  [6:0] iw_opcode,
  input  [6:0] opcode,
  input  [2:0] iw_funct3,
  input  [2:0] funct3,
  output eq
);

  wire i_type_jalr_eq, jalr_eq;

  Comparator #(.Bits(7)) i_type_jalr (.a(iw_opcode), .b(opcode), .eq(i_type_jalr_eq));  // open: gt, lt
  Comparator #(.Bits(3)) jalr (.a(iw_funct3), .b(funct3), .eq(jalr_eq));  // open: gt, lt
  and and_1 (eq, i_type_jalr_eq, jalr_eq);
endmodule
