// Digital circuit LOAD.dig as structural Verilog
module LOAD (
  input  [63:0] D,
  input  [63:0] TA,
  input  [1:0] MSZ,
  output [63:0] Dout
);

  wire [7:0] multiplexer_2_out;
  wire [31:0] multiplexer_1_out;
  wire [63:0] _64_BITS_2_out, _64_BITS_out;

  Multiplexer #(.Bits(32)) multiplexer_1 (.sel(TA[2]), .in_0(D[31:0]), .in_1(D[63:32]), .out(multiplexer_1_out));
  Multiplexer #(.Selector_Bits(3), .Bits(8)) multiplexer_2 (
    .sel(TA[2:0]), .in_0(D[7:0]), .in_1(D[15:8]), .in_2(D[23:16]), .in_3(D[31:24]), .in_4(D[39:32]),
    .in_5(D[47:40]), .in_6(D[55:48]), .in_7(D[63:56]), .out(multiplexer_2_out));
  BitExtender #(.inputBits(32), .outputBits(64)) _64_BITS (.in(multiplexer_1_out), .out(_64_BITS_out));
  BitExtender #(.outputBits(64)) _64_BITS_2 (.in(multiplexer_2_out), .out(_64_BITS_2_out));
  Multiplexer #(.Selector_Bits(2), .Bits(64)) multiplexer_3 (
    .sel(MSZ), .in_0(D), .in_1(_64_BITS_out), .in_2(_64_BITS_2_out), .in_3({64{1'b0}}), .out(Dout));
endmodule
