// Digital circuit MUL.dig as structural Verilog
module MUL (
  input  [6:0] iw_opcode,
  input  [2:0] iw_funct3,
  input  [6:0] opcode,
  input  [2:0] funct3,
  output eq
);

  wire mul_eq, r_type_eq;

  Comparator #(.Bits(7)) r_type (.a(iw_opcode), .b(opcode), .eq(r_type_eq));  // open: gt, lt
  Comparator #(.Bits(3)) mul (.a(iw_funct3), .b(funct3), .eq(mul_eq));  // open: gt, lt
  and and_1 (eq, r_type_eq, mul_eq);
endmodule
