// Digital circuit SB.dig as structural Verilog
module SB (
  input  [6:0] OPC,
  input  [2:0] funct3,
  output eq
);

  wire SB_2_eq, SB_eq;

  Comparator #(.Bits(7)) SB (.a(OPC), .b(7'b0100011), .eq(SB_eq));  // open: gt, lt
  Comparator #(.Bits(3)) SB_2 (.a(funct3), .b(3'b000), .eq(SB_2_eq));  // open: gt, lt
  and and_1 (eq, SB_eq, SB_2_eq);
endmodule
