// Digital circuit SLLI.dig as structural Verilog
module SLLI (
  input  [6:0] OPC,
  input  [2:0] funct3,
  output eq
);

  wire comparator_1_eq, SLLI_eq;

  Comparator #(.Bits(7)) SLLI (.a(OPC), .b(7'b0010011), .eq(SLLI_eq));  // open: gt, lt
  Comparator #(.Bits(3)) comparator_1 (.a(funct3), .b(3'b001), .eq(comparator_1_eq));  // open: gt, lt
  and and_1 (eq, SLLI_eq, comparator_1_eq);
endmodule
