// Digital circuit SRAI_Inst.dig as structural Verilog
module SRAI_Inst (
  input  [6:0] OPC,
  input  [2:0] funct3,
  input  [6:0] funct7,
  output R
);

  wire comparator_1_eq, comparator_2_eq, SRAI_eq;

  Comparator #(.Bits(7)) SRAI (.a(OPC), .b(7'b0010011), .eq(SRAI_eq));  // open: gt, lt
  Comparator #(.Bits(3)) comparator_1 (.a(funct3), .b(3'b101), .eq(comparator_1_eq));  // open: gt, lt
  Comparator #(.Bits(7)) comparator_2 (.a(funct7), .b(7'b0100000), .eq(comparator_2_eq));  // open: gt, lt
  and and_1 (R, SRAI_eq, comparator_1_eq, comparator_2_eq);
endmodule
