// Digital circuit Store.dig as structural Verilog
module Store (
  input  [63:0] Dout,
  input  [63:0] RD1,
  input  [1:0] MSZ,
  input  [63:0] TA,
  output [63:0] Din
);

  wire [63:0] multiplexer_1_out, multiplexer_2_out;

  Multiplexer #(.Selector_Bits(3), .Bits(64)) multiplexer_1 (
    .sel(TA[2:0]), .in_0({Dout[63:8], RD1[7:0]}), .in_1({Dout[63:16], RD1[7:0], Dout[7:0]}),
    .in_2({Dout[63:24], RD1[7:0], Dout[15:0]}), .in_3({Dout[63:32], RD1[7:0], Dout[23:0]}),
    .in_4({Dout[63:40], RD1[7:0], Dout[31:0]}), .in_5({Dout[63:48], RD1[7:0], Dout[39:0]}),
    .in_6({Dout[63:56], RD1[7:0], Dout[47:0]}), .in_7({RD1[7:0], Dout[55:0]}), .out(multiplexer_1_out));
  Multiplexer #(.Bits(64)) multiplexer_2 (
    .sel(TA[2]), .in_0({Dout[63:32], RD1[31:0]}), .in_1({Dout[31:0], RD1[31:0]}), .out(multiplexer_2_out));
  Multiplexer #(.Selector_Bits(2), .Bits(64)) multiplexer_3 (
    .sel(MSZ), .in_0(RD1), .in_1(multiplexer_2_out), .in_2(multiplexer_1_out), .in_3({64{1'b0}}), .out(Din));

  // Other names for the same wires on the sheet: w0[31:0] = Dout[31:0]; wb0[7:0] = Dout[7:0]; wb1[7:0] = Dout[15:8];
  //   wb2[7:0] = Dout[23:16]; wb3[7:0] = Dout[31:24]; w1[31:0] = Dout[63:32]; wb4[7:0] = Dout[39:32];
  //   wb5[7:0] = Dout[47:40]; wb6[7:0] = Dout[55:48]; wb7[7:0] = Dout[63:56]; wbn[7:0] = RD1[7:0];
  //   wn[31:0] = RD1[31:0]
endmodule
