// Digital circuit instruction-memory.dig as structural Verilog
module instruction_memory (
  input  [7:0] ADDR,
  input  PROG,
  output [31:0] IW
);

  wire [31:0] first_d, second_d;

  ROM #(.AddrBits(8), .Bits(32)) first (.A(ADDR), .sel(1'b1), .D(first_d));
  ROM #(.AddrBits(8), .Bits(32)) second (.A(ADDR), .sel(1'b1), .D(second_d));
  Multiplexer #(.Bits(32)) multiplexer_1 (.sel(PROG), .in_0(first_d), .in_1(second_d), .out(IW));

  // Notes on the sheet:
  //   contents of first (hex, n*v repeats v):
  //   100513,200593,b50633,c0001073
  //   contents of second (hex, n*v repeats v):
  //   100513,200593,8000ef,c0001073,b50533,8067
endmodule
