// Digital circuit project06.dig as structural Verilog
module project06 (
  input  CLK,
  input  [4:0] PROG,
  input  EN,
  input  CLR,
  output [63:0] A0,
  output [63:0] A1,
  output [63:0] A2,
  output DONE,
  output [63:0] A3
);

  wire _64_bit_register_1_p6, ALUSrcA, and_2_out, CLK_t, MLD, MST, PCbr, RFW, x1, x2, x3, x4, x5, x6, x7, x8,
       x9, x14, x15, x16, x17, x18, x19, x20, x21, x22, x23, x24, x25, x26, x27, x28, x29, x30, x31;
  wire [1:0] BROp, MSZ, PCsel, WDsel;
  wire [2:0] ALUSrcB;
  wire [3:0] ALUOp;
  wire [4:0] rd, rs1, rs2;
  wire [31:0] iw;
  wire [63:0] Dout, imm_B, imm_I, immdecoder_1_imm_j, immdecoder_1_imm_s, multiplexer_1_out,
       multiplexer_2_out, multiplexer_3_out, multiplexer_4_out, multiplexer_5_out, PC, PC_plus_4_s,
       ramdualport_1_d, RD0, RD1, store_1_din, TA;

  Multiplexer #(.Bits(64)) multiplexer_1 (.sel(PCbr), .in_0(PC_plus_4_s), .in_1(TA), .out(multiplexer_1_out));
  Multiplexer #(.Selector_Bits(2), .Bits(64)) multiplexer_2 (
    .sel(PCsel), .in_0(PC_plus_4_s), .in_1(TA), .in_2(multiplexer_1_out), .in_3({64{1'b0}}),
    .out(multiplexer_2_out));
  and and_1 (CLK_t, CLK, ~DONE);  // And
  Comparator #(.Bits(32)) End (.a(iw), .b(32'hc0001073), .eq(DONE));  // open: gt, lt
  // _64_bit_register _64_bit_register_1: pin names not known; wires that end beside it: multiplexer_2_out, CLK_t, EN, CLR, PC, _64_bit_register_1_p6, _64_bit_register_1_p6
  // Probe on PC
  // Probe on iw
  // Probe on rs1
  // Probe on rs2
  // Probe on rd
  // Probe on imm_I
  LED led_1 (.in(DONE));
  inst_mem inst_mem_1 (.PROG(PROG), .ADDR(PC[10:2]), .IW(iw));
  Add #(.Bits(64)) PC_plus_4 (.a(PC), .b(64'h4), .c_i(1'b0), .s(PC_plus_4_s));  // open: c_o
  // Probe on x1
  // Probe on x2
  // Probe on x3
  // Probe on x4
  // Probe on x5
  // Probe on x6
  // Probe on x7
  ImmDecoder immdecoder_1 (
    .IW(iw), .imm_I(imm_I), .imm_S(immdecoder_1_imm_s), .imm_B(imm_B), .imm_J(immdecoder_1_imm_j));  // open: imm_U
  InstDecoder instdecoder_1 (
    .IW(iw), .MSZ(MSZ), .MLD(MLD), .MST(MST), .BROp(BROp), .WDsel(WDsel), .PCsel(PCsel), .ALUSrcB(ALUSrcB),
    .ALUSrcA(ALUSrcA), .ALUOp(ALUOp), .RFW(RFW));
  RegDecoder regdecoder_1 (.IW(iw), .RS1(rs1), .RS2(rs2), .RD(rd));
  // Probe on x8
  // Probe on x9
  // Probe on A0
  // Probe on A1
  // Probe on A2
  // Probe on A3
  // Probe on x14
  // Probe on x15
  and and_2 (and_2_out, RFW, EN);
  Multiplexer #(.Selector_Bits(2), .Bits(64)) multiplexer_3 (
    .sel(WDsel), .in_0(TA), .in_1(PC_plus_4_s), .in_2(Dout), .in_3({64{1'b0}}), .out(multiplexer_3_out));
  // Probe on x16
  // Probe on x17
  // Probe on x18
  // Probe on x19
  // Probe on x20
  // Probe on x21
  // Probe on x22
  // Probe on x23
  // register_file register_file_1: pin names not known; wires that end beside it: rs1, rs2, rd, and_2_out, multiplexer_3_out, CLK_t, CLR, RD0, RD1, x1, x2, x3, x4, x5, x6, x7, x8, x9, A0, A1, A2, A3, x14, x15, x16, x17, x18, x19, x20, x21
  BU bu_1 (.RD0(RD0), .RD1(RD1), .PCbr(PCbr), .BRop(BROp));
  // Probe on x24
  // Probe on x25
  // Probe on x26
  // Probe on x27
  // Probe on x28
  // Probe on x29
  // Probe on x30
  // Probe on x31
  Store store_1 (.Din(store_1_din), .RD1(RD1), .Dout(ramdualport_1_d), .MSZ(MSZ), .TA(TA));
  Multiplexer #(.Bits(64)) multiplexer_4 (.sel(ALUSrcA), .in_0(RD0), .in_1(PC), .out(multiplexer_4_out));
  Multiplexer #(.Selector_Bits(3), .Bits(64)) multiplexer_5 (
    .sel(ALUSrcB), .in_0(RD1), .in_1(imm_I), .in_2(imm_B), .in_3(immdecoder_1_imm_j),
    .in_4(immdecoder_1_imm_s), .in_5({64{1'b0}}), .in_6({64{1'b0}}), .in_7({64{1'b0}}),
    .out(multiplexer_5_out));
  alu alu_1 (.A(multiplexer_4_out), .B(multiplexer_5_out), .ALUOp(ALUOp), .R(TA));
  RAMDualPort #(.AddrBits(7), .Bits(64)) ramdualport_1 (
    .A(TA[9:3]), .Din(store_1_din), .str(MST), .C(CLK_t), .ld(MLD), .D(ramdualport_1_d));
  LOAD load_1 (.TA(TA), .D(ramdualport_1_d), .MSZ(MSZ), .Dout(Dout));

  // Other names for the same wires on the sheet: x10[63:0] = A0; x11[63:0] = A1; x12[63:0] = A2; x13[63:0] = A3

  // Notes on the sheet:
  //   PASSING
endmodule

/* Test case 00-unit-add-i:
CLR EN CLK PROG A0 A1 A2 A3
1   0   0   x    x    x    x    x
0   0   0   x    x    x    x    x
while (!(DONE))
0   1   C   0    x    x    x    x
end while
0   1   0   0 3  0  0  0
*/

/* Test case 01-unit-add-r:
CLR EN CLK PROG A0 A1 A2 A3
1   0   0   x    x    x    x    x
0   0   0   x    x    x    x    x
while (!(DONE))
0   1   C   1    x    x    x    x
end while
0   1   0   1 9  6  0  0
*/

/* Test case 02-unit-jal:
CLR EN CLK PROG A0 A1 A2 A3
1   0   0   x    x    x    x    x
0   0   0   x    x    x    x    x
while (!(DONE))
0   1   C   2    x    x    x    x
end while
0   1   0   2 3  2  0  0
*/

/* Test case 03-unit-mul:
CLR EN CLK PROG A0 A1 A2 A3
1   0   0   x    x    x    x    x
0   0   0   x    x    x    x    x
while (!(DONE))
0   1   C   3    x    x    x    x
end while
0   1   0   3 21  7  0  0
*/

/* Test case 04-unit-sll-r:
CLR EN CLK PROG A0 A1 A2 A3
1   0   0   x    x    x    x    x
0   0   0   x    x    x    x    x
while (!(DONE))
0   1   C   4    x    x    x    x
end while
0   1   0   4 4  1  2  0
*/

/* Test case 05-unit-srl-r:
CLR EN CLK PROG A0 A1 A2 A3
1   0   0   x    x    x    x    x
0   0   0   x    x    x    x    x
while (!(DONE))
0   1   C   5    x    x    x    x
end while
0   1   0   5 4  8  1  0
*/

/* Test case 06-unit-slli:
CLR EN CLK PROG A0 A1 A2 A3
1   0   0   x    x    x    x    x
0   0   0   x    x    x    x    x
while (!(DONE))
0   1   C   6    x    x    x    x
end while
0   1   0   6 8  1  0  0
*/

/* Test case 07-unit-srli:
CLR EN CLK PROG A0 A1 A2 A3
1   0   0   x    x    x    x    x
0   0   0   x    x    x    x    x
while (!(DONE))
0   1   C   7    x    x    x    x
end while
0   1   0   7 8  32  0  0
*/

/* Test case 08-unit-j:
CLR EN CLK PROG A0 A1 A2 A3
1   0   0   x    x    x    x    x
0   0   0   x    x    x    x    x
while (!(DONE))
0   1   C   8    x    x    x    x
end while
0   1   0   8 1  0  0  0
*/

/* Test case 09-unit-beq:
CLR EN CLK PROG A0 A1 A2 A3
1   0   0   x    x    x    x    x
0   0   0   x    x    x    x    x
while (!(DONE))
0   1   C   9    x    x    x    x
end while
0   1   0   9 1  1  0  0
*/

/* Test case 10-unit-blt:
CLR EN CLK PROG A0 A1 A2 A3
1   0   0   x    x    x    x    x
0   0   0   x    x    x    x    x
while (!(DONE))
0   1   C   10    x    x    x    x
end while
0   1   0   10 1  2  0  0
*/

/* Test case 11-unit-bge:
CLR EN CLK PROG A0 A1 A2 A3
1   0   0   x    x    x    x    x
0   0   0   x    x    x    x    x
while (!(DONE))
0   1   C   11    x    x    x    x
end while
0   1   0   11 2  1  0  0
*/

/* Test case 12-unit-sd-ld:
CLR EN CLK PROG A0 A1 A2 A3
1   0   0   x    x    x    x    x
0   0   0   x    x    x    x    x
while (!(DONE))
0   1   C   12    x    x    x    x
end while
0   1   0   12 99  0  0  0
*/

/* Test case 13-unit-sw-lw:
CLR EN CLK PROG A0 A1 A2 A3
1   0   0   x    x    x    x    x
0   0   0   x    x    x    x    x
while (!(DONE))
0   1   C   13    x    x    x    x
end while
0   1   0   13 99  0  0  0
*/

/* Test case 14-unit-sb-lb:
CLR EN CLK PROG A0 A1 A2 A3
1   0   0   x    x    x    x    x
0   0   0   x    x    x    x    x
while (!(DONE))
0   1   C   14    x    x    x    x
end while
0   1   0   14 99  0  0  0
*/

/* Test case 15-prog-quadratic:
CLR EN CLK PROG A0 A1 A2 A3
1   0   0   x    x    x    x    x
0   0   0   x    x    x    x    x
while (!(DONE))
0   1   C   15    x    x    x    x
end while
0   1   0   15 25  3  4  5
*/

/* Test case 16-prog-get-bitseq:
CLR EN CLK PROG A0 A1 A2 A3
1   0   0   x    x    x    x    x
0   0   0   x    x    x    x    x
while (!(DONE))
0   1   C   16    x    x    x    x
end while
0   1   0   16 6  12  15  0
*/

/* Test case 17-prog-fibrec:
CLR EN CLK PROG A0 A1 A2 A3
1   0   0   x    x    x    x    x
0   0   0   x    x    x    x    x
while (!(DONE))
0   1   C   17    x    x    x    x
end while
0   1   0   17 55  0  0  0
*/

/* Test case 19-prog-to-upper:
CLR EN CLK PROG A0 A1 A2 A3
1   0   0   x    x    x    x    x
0   0   0   x    x    x    x    x
while (!(DONE))
0   1   C   19    x    x    x    x
end while
0   1   0   19 5066355251797426176  1014  0  0
*/

/* Test case 18-prog-is-pal:
CLR EN CLK PROG A0 A1 A2 A3
1   0   0   x    x    x    x    x
0   0   0   x    x    x    x    x
while (!(DONE))
0   1   C   18    x    x    x    x
end while
0   1   0   18 1  3  3  0
*/

/* Test case 20-prog-swap:
CLR EN CLK PROG A0 A1 A2 A3
1   0   0   x    x    x    x    x
0   0   0   x    x    x    x    x
while (!(DONE))
0   1   C   20    x    x    x    x
end while
0   1   0   20 12  1  5  0
*/

/* Test case 21-prog-sort:
CLR EN CLK PROG A0 A1 A2 A3
1   0   0   x    x    x    x    x
0   0   0   x    x    x    x    x
while (!(DONE))
0   1   C   21    x    x    x    x
end while
0   1   0   21 8589934596  25769803784  42949672972  0
*/
