// Digital circuit 2-bit-register-clr-en.dig as structural Verilog
module _2_bit_register_clr_en (
  input  [1:0] D,
  input  CLK,
  input  EN,
  input  CLR,
  output [1:0] Q
);

  _1_bit_register _1_bit_register_1 (.D(D[0]), .CLK(CLK), .EN(EN), .CLR(CLR), .Q(Q[0]));  // open: nQ
  _1_bit_register _1_bit_register_2 (.D(D[1]), .CLK(CLK), .EN(EN), .CLR(CLR), .Q(Q[1]));  // open: nQ
endmodule
