// Digital circuit 32-bit-register-clr-en.dig as structural Verilog
module _32_bit_register_clr_en (
  input  [31:0] D,
  input  CLK,
  input  EN,
  input  CLR,
  output [31:0] Q
);

  _8bit_register_clr_en _8bit_register_clr_en_1 (.D(D[7:0]), .CLK(CLK), .EN(EN), .CLR(CLR), .Q(Q[7:0]));
  _8bit_register_clr_en _8bit_register_clr_en_2 (.D(D[15:8]), .CLK(CLK), .EN(EN), .CLR(CLR), .Q(Q[15:8]));
  _8bit_register_clr_en _8bit_register_clr_en_3 (.D(D[23:16]), .CLK(CLK), .EN(EN), .CLR(CLR), .Q(Q[23:16]));
  _8bit_register_clr_en _8bit_register_clr_en_4 (.D(D[31:24]), .CLK(CLK), .EN(EN), .CLR(CLR), .Q(Q[31:24]));
endmodule
