// Digital circuit 8bit-register-clr-en.dig as structural Verilog
module _8bit_register_clr_en (
  input  [7:0] D,
  input  CLK,
  input  EN,
  input  CLR,
  output [7:0] Q
);

  _4bit_register_clr_en _4bit_register_clr_en_1 (.D(D[3:0]), .CLK(CLK), .EN(EN), .CLR(CLR), .Q(Q[3:0]));
  _4bit_register_clr_en _4bit_register_clr_en_2 (.D(D[7:4]), .CLK(CLK), .EN(EN), .CLR(CLR), .Q(Q[7:4]));
endmodule
