// Digital circuit ADDR.dig as structural Verilog
module ADDR (
  input  [6:0] iw_opcode,
  input  [2:0] iw_funct3,
  input  [6:0] iw_funct7,
  output eq
);

  wire add3_eq, add7_eq, r_type_eq;

  Comparator #(.Bits(7)) r_type (.a(iw_opcode), .b(7'b0110011), .eq(r_type_eq));  // open: gt, lt
  Comparator #(.Bits(3)) add3 (.a(iw_funct3), .b(3'b000), .eq(add3_eq));  // open: gt, lt
  Comparator #(.Bits(7)) add7 (.a(iw_funct7), .b({7{1'b0}}), .eq(add7_eq));  // open: gt, lt
  and and_1 (eq, r_type_eq, add3_eq, add7_eq);
endmodule
