// Digital circuit LB.dig as structural Verilog
module LB (
  input  [6:0] OPC,
  input  [2:0] funct3,
  output eq
);

  wire comparator_1_eq, LB_eq;

  Comparator #(.Bits(7)) LB (.a(OPC), .b(7'b0000011), .eq(LB_eq));  // open: gt, lt
  Comparator #(.Bits(3)) comparator_1 (.a(funct3), .b(3'b000), .eq(comparator_1_eq));  // open: gt, lt
  and and_1 (eq, LB_eq, comparator_1_eq);
endmodule
