// Digital circuit LD.dig as structural Verilog
module LD (
  input  [6:0] OPC,
  input  [2:0] funct3,
  output eq
);

  wire comparator_1_eq, LD_eq;

  Comparator #(.Bits(7)) LD (.a(OPC), .b(7'b0000011), .eq(LD_eq));  // open: gt, lt
  Comparator #(.Bits(3)) comparator_1 (.a(funct3), .b(3'b011), .eq(comparator_1_eq));  // open: gt, lt
  and and_1 (eq, LD_eq, comparator_1_eq);
endmodule
