// Digital circuit LW.dig as structural Verilog
module LW (
  input  [6:0] OPC,
  input  [2:0] funct3,
  output eq
);

  wire comparator_1_eq, LW_eq;

  Comparator #(.Bits(7)) LW (.a(OPC), .b(7'b0000011), .eq(LW_eq));  // open: gt, lt
  Comparator #(.Bits(3)) comparator_1 (.a(funct3), .b(3'b010), .eq(comparator_1_eq));  // open: gt, lt
  and and_1 (eq, LW_eq, comparator_1_eq);
endmodule
