// Digital circuit SD.dig as structural Verilog
module SD (
  input  [6:0] OPC,
  input  [2:0] funct3,
  output eq
);

  wire SD_2_eq, SD_eq;

  Comparator #(.Bits(7)) SD (.a(OPC), .b(7'b0100011), .eq(SD_eq));  // open: gt, lt
  Comparator #(.Bits(3)) SD_2 (.a(funct3), .b(3'b011), .eq(SD_2_eq));  // open: gt, lt
  and and_1 (eq, SD_eq, SD_2_eq);
endmodule
