// Digital circuit SUB.dig as structural Verilog
module SUB (
  input  [6:0] OPC,
  input  [2:0] funct3,
  input  [6:0] funct7,
  output eq
);

  wire ADDR_eq, comparator_1_eq, comparator_2_eq;

  Comparator #(.Bits(7)) ADDR (.a(OPC), .b(7'b0110011), .eq(ADDR_eq));  // open: gt, lt
  Comparator #(.Bits(3)) comparator_1 (.a(funct3), .b(3'b000), .eq(comparator_1_eq));  // open: gt, lt
  Comparator #(.Bits(7)) comparator_2 (.a(funct7), .b(7'b0100000), .eq(comparator_2_eq));  // open: gt, lt
  and and_1 (eq, ADDR_eq, comparator_1_eq, comparator_2_eq);
endmodule
