// Digital circuit SW.dig as structural Verilog
module SW (
  input  [6:0] OPC,
  input  [2:0] funct3,
  output eq
);

  wire SW_2_eq, SW_eq;

  Comparator #(.Bits(7)) SW (.a(OPC), .b(7'b0100011), .eq(SW_eq));  // open: gt, lt
  Comparator #(.Bits(3)) SW_2 (.a(funct3), .b(3'b010), .eq(SW_2_eq));  // open: gt, lt
  and and_1 (eq, SW_eq, SW_2_eq);
endmodule
