// Digital circuit alu.dig as structural Verilog
module alu (
  input  [63:0] A,
  input  [63:0] B,
  input  [2:0] ALUOp,
  output [63:0] R
);

  wire [63:0] add_s, and_1_out, mul_mul, or_1_out, sll_out, srai_out, srl_out, sub_s;

  Add #(.Bits(64)) add (.a(A), .b(B), .c_i(1'b0), .s(add_s));  // open: c_o
  Mul #(.Bits(32)) mul (.a(A[31:0]), .b(B[31:0]), .mul(mul_mul));
  Sub #(.Bits(64)) sub (.a(A), .b(B), .c_i(1'b0), .s(sub_s));  // open: c_o
  BarrelShifter #(.Bits(64)) sll (.in(A), .shift(B[6:0]), .out(sll_out));
  BarrelShifter #(.Bits(64), .direction("right")) srl (.in(A), .shift(B[6:0]), .out(srl_out));
  BarrelShifter #(.Bits(64), .barrelShifterMode("arithmetic"), .direction("right")) srai (
    .in(A), .shift(B[6:0]), .out(srai_out));
  assign and_1_out = A & B;  // And and_1, 64 bits wide
  assign or_1_out = A | B;  // Or or_1, 64 bits wide
  Multiplexer #(.Selector_Bits(3), .Bits(64)) multiplexer_1 (
    .sel(ALUOp), .in_0(add_s), .in_1(mul_mul), .in_2(sub_s), .in_3(sll_out), .in_4(srl_out), .in_5(srai_out),
    .in_6(and_1_out), .in_7(or_1_out), .out(R));
endmodule
