// Digital circuit d-latch-clr.dig as structural Verilog
module d_latch_clr (
  input  D,
  input  CLK,
  input  CLR,
  output Q,
  output nQ
);

  wire and_1_out, and_2_out, and_3_out, or_1_out;

  and and_1 (and_1_out, D, ~CLR);  // And
  or or_1 (or_1_out, CLK, CLR);
  and and_2 (and_2_out, ~and_1_out, or_1_out);  // And
  and and_3 (and_3_out, and_1_out, or_1_out);
  sr_latch sr_latch_1 (.R(and_2_out), .S(and_3_out), .Q(Q), .nQ(nQ));
endmodule
