// Digital circuit sr-latch.dig as structural Verilog
module sr_latch (
  input  R,
  input  S,
  output Q,
  output nQ
);

  nor nor_1 (Q, R, nQ);
  nor nor_2 (nQ, Q, S);

  // Notes on the sheet:
  //   SR Latch
endmodule
